// Logisim project mahadha.circ as structural Verilog: 4 circuits, main circuit main
module main (
  input  in_1,
  input  X0,
  input  X1,
  input  X2,
  input  X3,
  output [7:0] positive_result,
  output [8:0] negative_reasult
);

  wire fuladder_1_cn_1, halvadder_1_c1, halvadder_2_c1;

  halvadder halvadder_1 (.A0(X0), .B0(X2), .S0(positive_result[3]), .C1(halvadder_1_c1));
  fuladder fuladder_1 (.An(halvadder_1_c1), .Bn(X1), .Cn(X3), .Sn(positive_result[4]), .Cn_1(fuladder_1_cn_1));
  halvadder halvadder_2 (.A0(fuladder_1_cn_1), .B0(X2), .S0(positive_result[5]), .C1(halvadder_2_c1));
  halvadder halvadder_3 (.A0(halvadder_2_c1), .B0(X3), .S0(positive_result[6]), .C1(positive_result[7]));
  negetor negetor_1 (.in_2({positive_result[7:3], X1, X0, in_1}), .Switch(1'b1), .out_3(negative_reasult));

  assign positive_result[2:0] = {X1, X0, in_1};

  // Notes on the sheet:
  //   Switch
endmodule

module halvadder (
  input  A0,
  input  B0,
  output S0,
  output C1
);

  xor xor_1 (S0, A0, B0);
  and and_1 (C1, A0, B0);
endmodule

module fuladder (
  input  An,
  input  Bn,
  input  Cn,
  output Sn,
  output Cn_1
);

  wire and_1_out, and_2_out, xor_1_out;

  xor xor_1 (xor_1_out, An, Bn);
  and and_1 (and_1_out, An, Bn);
  xor xor_2 (Sn, xor_1_out, Cn);
  and and_2 (and_2_out, xor_1_out, Cn);
  or or_1 (Cn_1, and_2_out, and_1_out);
endmodule

module negetor (
  input  Switch,
  input  [7:0] in_2,
  output [8:0] out_3
);

  wire halvadder_2_c1, halvadder_3_c1, halvadder_4_c1, halvadder_5_c1, halvadder_6_c1, halvadder_7_c1,
       halvadder_8_c1, xor_1_out, xor_2_out, xor_3_out, xor_4_out, xor_5_out, xor_6_out, xor_7_out, xor_8_out;

  xor xor_1 (xor_1_out, in_2[7], Switch);
  halvadder halvadder_1 (.A0(halvadder_2_c1), .B0(xor_1_out), .S0(out_3[7]), .C1(out_3[8]));
  xor xor_2 (xor_2_out, in_2[6], Switch);
  halvadder halvadder_2 (.A0(halvadder_3_c1), .B0(xor_2_out), .S0(out_3[6]), .C1(halvadder_2_c1));
  xor xor_3 (xor_3_out, in_2[5], Switch);
  halvadder halvadder_3 (.A0(halvadder_4_c1), .B0(xor_3_out), .S0(out_3[5]), .C1(halvadder_3_c1));
  xor xor_4 (xor_4_out, in_2[4], Switch);
  halvadder halvadder_4 (.A0(halvadder_5_c1), .B0(xor_4_out), .S0(out_3[4]), .C1(halvadder_4_c1));
  xor xor_5 (xor_5_out, in_2[3], Switch);
  halvadder halvadder_5 (.A0(halvadder_6_c1), .B0(xor_5_out), .S0(out_3[3]), .C1(halvadder_5_c1));
  xor xor_6 (xor_6_out, in_2[2], Switch);
  halvadder halvadder_6 (.A0(halvadder_7_c1), .B0(xor_6_out), .S0(out_3[2]), .C1(halvadder_6_c1));
  xor xor_7 (xor_7_out, in_2[1], Switch);
  halvadder halvadder_7 (.A0(halvadder_8_c1), .B0(xor_7_out), .S0(out_3[1]), .C1(halvadder_7_c1));
  xor xor_8 (xor_8_out, in_2[0], Switch);
  halvadder halvadder_8 (.A0(Switch), .B0(xor_8_out), .S0(out_3[0]), .C1(halvadder_8_c1));

  // Notes on the sheet:
  //   positive input
  //   negative output
endmodule
