// Logisim project oblig-to.circ as structural Verilog: 4 circuits, main circuit counter
module main (
  input  in_1,
  input  in_2,
  output [3:0] out_3
);

  wire clk, decoder_1_lsb, decoder_1_msb, decoder_1_out_4, decoder_1_out_5, or_1_out, or_2_out, or_3_out;
  wire [3:0] controlled_buffer_1_out, controlled_buffer_2_out, register_1_q, register_1_q_2;
  wire [7:0] ram_1_data;

  counter counter_1 (.Counter(clk), .Reset(in_2), .out_3(out_3));
  RAM #(.addrWidth(4)) ram_1 (.addr(out_3), .data(ram_1_data), .clr(in_1));  // open: sel, clk, ld
  decoder decoder_1 (
    .Input(ram_1_data[7:4]), .LSB(decoder_1_lsb), .MSB(decoder_1_msb), .out_4(decoder_1_out_4),
    .out_5(decoder_1_out_5));
  assign controlled_buffer_1_out = decoder_1_lsb ? ram_1_data[3:0] : 4'bz;  // Controlled_Buffer controlled_buffer_1
  assign controlled_buffer_2_out = decoder_1_msb ? ram_1_data[3:0] : 4'bz;  // Controlled_Buffer controlled_buffer_2
  or or_1 (or_1_out, decoder_1_lsb, decoder_1_out_5);
  or or_2 (or_2_out, decoder_1_msb, decoder_1_out_5);
  or or_3 (or_3_out, decoder_1_out_4, decoder_1_out_5);
  assign controlled_buffer_2_out = or_1_out ? register_1_q_2 : 4'bz;  // Controlled_Buffer controlled_buffer_3
  Register register_1 (
    .D({controlled_buffer_2_out, controlled_buffer_1_out}), .Q({register_1_q_2, register_1_q}), .clk(clk),
    .clr(in_1));  // open: en
  assign controlled_buffer_1_out = or_2_out ? register_1_q : 4'bz;  // Controlled_Buffer controlled_buffer_4
  Clock clock_1 (.out(clk));
  RAM #(.addrWidth(4)) ram_2 (
    .addr(ram_1_data[3:0]), .data({controlled_buffer_2_out, controlled_buffer_1_out}), .sel(or_3_out),
    .clk(clk), .ld(decoder_1_out_4), .clr(in_1));

  // Other names for the same wires on the sheet: clear = in_1

  // Notes on the sheet:
  //   Counter
  //   Program mine
  //   Decoder
  //   lsb
  //   msb
  //   wd
  //   ld
  //   R
  //   Data mine
endmodule

module counter (
  input  Counter,
  input  Reset,
  output [3:0] out_3
);

  wire halvadder_1_c1, halvadder_2_c1, halvadder_3_c1, halvadder_4_c1, not_1_out;
  wire [3:0] register_1_q;

  Halvadder halvadder_1 (.A0(register_1_q[0]), .B0(1'b1), .S0(out_3[0]), .C1(halvadder_1_c1));
  // Probe on register_1_q
  Halvadder halvadder_2 (.A0(register_1_q[1]), .B0(halvadder_1_c1), .S0(out_3[1]), .C1(halvadder_2_c1));
  Halvadder halvadder_3 (.A0(register_1_q[2]), .B0(halvadder_2_c1), .S0(out_3[2]), .C1(halvadder_3_c1));
  Register #(.width(4), .trigger("falling")) register_1 (
    .D(out_3), .en(not_1_out), .Q(register_1_q), .clk(Counter), .clr(Reset));
  not not_1 (not_1_out, halvadder_4_c1);
  Halvadder halvadder_4 (.A0(register_1_q[3]), .B0(halvadder_3_c1), .S0(out_3[3]), .C1(halvadder_4_c1));
  // Probe on out_3

  // Notes on the sheet:
  //   Input
  //   Register
  //   Output
endmodule

module decoder (
  input  [3:0] Input,
  output LSB,
  output MSB,
  output out_4,
  output out_5
);

  wire not_1_out, not_2_out, not_3_out;

  not not_1 (not_1_out, Input[0]);
  not not_2 (not_2_out, Input[1]);
  not not_3 (not_3_out, Input[2]);
  and _1000 (LSB, not_1_out, not_2_out, not_3_out, Input[3]);
  and _1001 (MSB, Input[0], not_2_out, not_3_out, Input[3]);
  and _1010 (out_4, not_1_out, Input[1], not_3_out, Input[3]);
  and _1011 (out_5, Input[0], Input[1], not_3_out, Input[3]);

  // Notes on the sheet:
  //   Load to dataminne
  //   write to Dataminne
endmodule

module Halvadder (
  input  A0,
  input  B0,
  output S0,
  output C1
);

  xor xor_1 (S0, A0, B0);
  and and_1 (C1, A0, B0);
endmodule
